# Fritzing sketch Teensy Gogogo Connection (saved by Fritzing 0.9.3b)
breadboards: 1

parts:
  LED1 = LED - 5mm [color="Green (555nm)" package="5 mm [THT]"]
  LED2 = LED - 5mm [color="Red (633nm)" package="5 mm [THT]"]
  LED3 = LED - 5mm [color="Red (633nm)" package="5 mm [THT]"]
  LED4 = LED - 5mm [color="Green (555nm)" package="5 mm [THT]"]
  LED5 = LED - 5mm [color="Red (633nm)" package="5 mm [THT]"]
  LED6 = LED - 5mm [color="Green (555nm)" package="5 mm [THT]"]
  LED7 = LED - 5mm [color="Red (633nm)" package="5 mm [THT]"]
  LED8 = LED - 5mm [color="Green (555nm)" package="5 mm [THT]"]
  LED9 = LED - 5mm [color="Green (555nm)" package="5 mm [THT]"]
  LED10 = LED - 5mm [color="Red (633nm)" package="5 mm [THT]"]
  Go_go_go1 = Go, go, go Motor controller
  Teensy1 = Teensy 3.1

nets:
  N1: LED1.cathode, LED2.anode, LED3.anode, LED4.cathode, LED5.anode, LED6.cathode, LED7.anode, LED8.cathode, LED9.cathode, LED10.anode, Go_go_go1.Out2
  N2: LED1.anode, LED2.cathode, LED3.cathode, LED4.anode, LED5.cathode, LED6.anode, LED7.cathode, LED8.anode, LED9.anode, LED10.cathode, Go_go_go1.Out1
  GND: Go_go_go1.GND, Teensy1.GND, Teensy1.D0, Teensy1.D1
  N3: Go_go_go1.Standby, Teensy1.D4
  N4: Go_go_go1.IN1, Teensy1.D5
  N5: Go_go_go1.IN2, Teensy1.D6
  N6: Go_go_go1.PWM, Teensy1.D3

notes:
  Lab power 3V3

custom parts:
  Teensy 3.1: The Teensy is a complete USB-based microcontoller development system, in a very small footprint, capable of implementing many types of projects. All programming is done via the USB port. No special programmer is needed, only a standard micro-USB cable and a PC or Macintosh with a USB port. It has a USB keyboard/mouse/joystick emulation stack and can be programmed through Arduino IDE.
